# Fritzing sketch theremin (saved by Fritzing 0.8.7b)
breadboards: 1

parts:
  Parte1 = Arduino Uno (Rev3)
  U1 = POT [package=pot_mammoth]
  Parte2 = SRF05 Ultrasonic Rangefinder

nets:
  N1: Parte1.A0, U1.A
  N2: Parte1.A5/SCL, Parte2.Echo
  N3: Parte1.D10_PWM/SS, Parte2.Trig
  N4: U1.S, Parte2.GND
  N5: U1.E, Parte2.VCC
